# Fritzing sketch rele 4 canais e botoes (saved by Fritzing 0.9.3b)
breadboards: 1

parts:
  Componente1 = Arduino Uno (Rev3)
  WeMos_D1_Mini_Relay_Shield_V1 = WeMos D1 Mini Relay Shield V2
  WeMos_D1_Mini_Relay_Shield_V2 = WeMos D1 Mini Relay Shield V2
  WeMos_D1_Mini_Relay_Shield_V3 = WeMos D1 Mini Relay Shield V2
  WeMos_D1_Mini_Relay_Shield_V4 = WeMos D1 Mini Relay Shield V2
  S1 = Pushbutton [package="[THT]"]
  S2 = Pushbutton [package="[THT]"]
  S3 = Pushbutton [package="[THT]"]
  S4 = Pushbutton [package="[THT]"]
  R1 = Resistor [tolerance=±5% resistance=220 package=THT]
  R2 = Resistor [tolerance=±5% resistance=220 package=THT]
  R3 = Resistor [tolerance=±5% resistance=220 package=THT]
  R4 = Resistor [tolerance=±5% resistance=220 package=THT]

nets:
  N1: Componente1.D8, WeMos_D1_Mini_Relay_Shield_V2.D6
  N2: Componente1.D9_PWM, WeMos_D1_Mini_Relay_Shield_V3.D5
  N3: Componente1.D10_PWM/SS, WeMos_D1_Mini_Relay_Shield_V4.D0
  N4: Componente1.D2, S1.Pin_1, S1.Pin_2, R1.Pin_1
  N5: Componente1.D3_PWM, S2.Pin_1, S2.Pin_2, R2.Pin_1
  N6: Componente1.D4, S3.Pin_1, S3.Pin_2, R3.Pin_1
  N7: Componente1.D5_PWM, S4.Pin_1, S4.Pin_2, R4.Pin_1
  N8: Componente1.D7, WeMos_D1_Mini_Relay_Shield_V1.D7
  5V: WeMos_D1_Mini_Relay_Shield_V1.5V, WeMos_D1_Mini_Relay_Shield_V2.5V, WeMos_D1_Mini_Relay_Shield_V3.5V, WeMos_D1_Mini_Relay_Shield_V4.5V, S1.Pin_3, S1.Pin_4, S2.Pin_3, S2.Pin_4, S3.Pin_3, S3.Pin_4, S4.Pin_3, S4.Pin_4
  N9: WeMos_D1_Mini_Relay_Shield_V1.G, WeMos_D1_Mini_Relay_Shield_V2.G, WeMos_D1_Mini_Relay_Shield_V3.G, WeMos_D1_Mini_Relay_Shield_V4.G, R1.Pin_0, R2.Pin_0, R3.Pin_0, R4.Pin_0
