# Fritzing sketch ACIONAMENTO Sketch 2 (saved by Fritzing 0.9.3b)
breadboards: 1

parts:
  Componente2 = Arduino Mega ADK (Rev3)
  U1 = 4-Channel 5v Relay Shield [package=relay-4ch5v10a]
  LCD2 = LCD screen
  LCM1602_IIC1 = LCM1602 IIC [part_number="LCM1602 IIC" chip_label="LCM1602 IIC" package="DIP (Dual Inline) [THT]"]
  LED1 = LED - 5mm [color="Blue (505nm)" package="5 mm [THT]"]
  LED2 = LED - 5mm [color="Red (633nm)" package="5 mm [THT]"]
  R1 = Resistor [tolerance=±5% resistance=220 package=THT]
  R2 = Resistor [tolerance=±5% resistance=220 package=THT]
  U2 = SLIDER [package=slider]
  J1 = Piezo Speaker
  DHT1 = DHT11_Temperature_and_Humitidy_Sensor
  PCB2 = RTC_DS1302_module
  S4 = Round Pushbutton
  S5 = Round Pushbutton

nets:
  N1: Componente2.A5, DHT1.connector1
  N2: Componente2.D21/SCL, LCM1602_IIC1.SCL
  N3: Componente2.D20/SDA, LCM1602_IIC1.SDA
  N4: Componente2.D18/TX1, U2.E
  N5: Componente2.D8_PWM, U1.IN2
  VCC: Componente2.5V, U1.VCC, U2.S, J1.pin2, DHT1.connector2, PCB2.VCC
  GND: Componente2.GND, U1.GND, LCM1602_IIC1.GND, R1.Pin_1, R2.Pin_0, U2.A, DHT1.connector3, PCB2.GND, S4.leg1, S5.leg1
  N6: Componente2.D3_PWM, S4.leg0
  N7: Componente2.D5_PWM, S5.leg0
  N8: Componente2.D6_PWM, U1.IN1
  N9: Componente2.D7_PWM, J1.pin1
  N10: Componente2.D31, PCB2.RST
  N11: Componente2.D33, PCB2.DAT
  N12: Componente2.D35, PCB2.CLK
  N13: U1.K1-Off, U1.K2-Off, LCM1602_IIC1.VCC
  N14: U1.K1-On, LED1.cathode
  N15: U1.K2-On, LED2.cathode
  VSS: LCD2.VSS, LCM1602_IIC1.VSS
  VDD: LCD2.VDD, LCM1602_IIC1.VDD
  N16: LCD2.V0, LCM1602_IIC1.V0
  N17: LCD2.RS, LCM1602_IIC1.RS
  N18: LCD2.R/W, LCM1602_IIC1.RW
  N19: LCD2.E, LCM1602_IIC1.E
  N20: LCD2.DB0, LCM1602_IIC1.D0
  N21: LCD2.DB1, LCM1602_IIC1.D1
  N22: LCD2.DB2, LCM1602_IIC1.D2
  N23: LCD2.DB3, LCM1602_IIC1.D3
  N24: LCD2.DB4, LCM1602_IIC1.D4
  N25: LCD2.DB5, LCM1602_IIC1.D5
  N26: LCD2.DB6, LCM1602_IIC1.D6
  N27: LCD2.DB7, LCM1602_IIC1.D7
  N28: LCD2.LED+, LCM1602_IIC1.A
  N29: LCD2.LED-, LCM1602_IIC1.K
  N30: LED1.anode, R1.Pin_0
  N31: LED2.anode, R2.Pin_1

notes:
  O fio do sinal inverte com o ground no sensor magnético (não encontrei um desenho exato do sensor)
  As saídas dos relés devem ainda ser ajustadas para o circuito, pois não conseguimos fazer mais testes com as contactoras e os relés do quadro
  o DHT11 usado tem 3 pinos
  caso for feitos novos testes, o circuito deve estar totalmente fechado, para que não se dispare o alarme, ou seja, deve-se testar com as saídas ligadas, ou LEDS

custom parts:
  4-Channel 5v Relay Shield: 4 Channel 5v Relay Shield w. 2x SPD-06VDC-SD-C
  LCM1602 IIC: I2C-Module to use a 1602 or 2004 LCD on with the wire.h libory Serial LCD Modul
  SLIDER: Slide-type potentiometer- COM-9119
  RTC_DS1302_module: Arduino module DS1302 SPI Real Time Clock
